// Logisim project Calculator.circ as structural Verilog: 11 circuits, main circuit main
module Calculator (
  input  in_1,
  input  in_2,
  input  OPERATION,
  input  in_4,
  input  in_5,
  input  in_6,
  input  in_7,
  input  in_8
);

  wire a, b, c, d, divider_flag, e, f, g, negative, zero_flag;

  Implementation implementation_1 (
    .in_1(in_6), .in_2(in_5), .in_3(in_4), .in_4(OPERATION), .in_5(in_2), .in_6(in_1), .a(a), .b(b), .c(c),
    .d(d), .e(e), .f(f), .g(g), .N(negative), .zero_flag(zero_flag), .divider_flag(divider_flag),
    .in_7(in_7), .in_8(in_8));
  _7_Segment_Display u_7_segment_display_1 (.g(negative));  // open: f, a, b, e, d, c, dp
  _7_Segment_Display u_7_segment_display_2 (.g(g), .f(f), .a(a), .b(b), .e(e), .d(d), .c(c));  // open: dp
  LED led_1 (.in(negative));
  LED led_2 (.in(zero_flag));
  LED led_3 (.in(divider_flag));

  // Other names for the same wires on the sheet: A0 = in_6; A1 = in_5; B0 = OPERATION; B1 = in_2; N0 = in_4;
  //   N1 = in_1; op0 = in_8; op1 = in_7

  // Notes on the sheet:
  //   0         0      -->     Addition
  //   0         1      -->     Addition
  //   1         0      -->     Multiplication
  //   1        1      -->     Division
endmodule

// ALU
module Implementation (
  input  in_1,
  input  in_2,
  input  in_3,
  input  in_4,
  input  in_5,
  input  in_6,
  input  in_7,
  input  in_8,
  output a,
  output b,
  output c,
  output d,
  output e,
  output f,
  output g,
  output N,
  output zero_flag,
  output divider_flag
);

  wire _0_flg, div, div_flag, minus_op0, minus_op1, mult, N_D, N_D_F, N_M, N_M_F, N_S, N_S_F, N_t, S0, S0_1,
       S0_D, S0_M, S0_S, S1, S1_1, S1_D, S1_M, S1_S, S2, S2_1, S2_M, S2_S, S3, S3_1, S3_M;

  Addition addition_1 (
    .in_1(in_1), .in_2(in_2), .in_3(in_3), .in_4(in_4), .in_5(in_5), .in_6(in_6), .out_7(S0_S), .out_8(S1_S),
    .out_9(S2_S), .out_10(N_S));
  Multiplication multiplication_1 (
    .in_1(in_1), .in_2(in_2), .in_3(in_3), .in_4(in_4), .in_5(in_5), .in_6(in_6), .S0(S0_M), .S1(S1_M),
    .S2(S2_M), .S3(S3_M), .N(N_M));
  Division division_1 (
    .in_1(in_1), .in_2(in_2), .in_3(in_3), .in_4(in_4), .in_5(in_5), .in_6(in_6), .S0(S0_D), .S1(S1_D),
    .zero_divider_flag(div_flag), .N(N_D));
  // _74157 74157_1: pin names not known; wires that end beside it: in_7, S0_S, S0_1, S0, S1_S, S1_1, S1, 1'b0, 1'b1, 1'b0, S2_S, S2_1, S2, 1'b0, S3_1, S3
  // _74157 74157_2: pin names not known; wires that end beside it: in_8, S0_M, S0_D, S0_1, S1_M, S1_D, S1_1, 1'b0, 1'b1, 1'b0, S2_M, 1'b0, S2_1, S3_M, 1'b0, S3_1
  // _744075 744075_1: pin names not known; wires that end beside it: S0, S1, 1'b0, 1'b1, S2, _0_flg, N_S_F, N_M_F, N_D_F, N_t
  // _7408 7408_1: pin names not known; wires that end beside it: in_7, in_8, div, in_7, minus_op0, mult, 1'b0, 1'b1, mult, N_M, N_M_F, div, N_D, N_D_F
  // _7404 7404_1: pin names not known; wires that end beside it: in_8, minus_op0, in_7, minus_op1, 1'b0, 1'b1
  // _7408 7408_2: pin names not known; wires that end beside it: div_flag, div, divider_flag, minus_op1, N_S, N_S_F, 1'b0, 1'b1, N_t, _0_flg, N, minus_op1, N_S, N_S_F
  not not_1 (zero_flag, _0_flg);
  // _7448 7448_1: pin names not known; wires that end beside it: S1, S2, 1'b1, 1'b1, 1'b1, S3, S0, 1'b0, 1'b1, f, g, a, b, c, d, e

  // Other names for the same wires on the sheet: A0 = in_1; A1 = in_2; B0 = in_4; B1 = in_5; N0 = in_3; N1 = in_6;
  //   N_F = N; op0 = in_8; op1 = in_7

  // Notes on the sheet:
  //   0    0      -->     Addition
  //   0    1      -->     Addition
  //   1    0      -->     Multiplication
  //   1    1      -->     Division
endmodule

module Multiplication (
  input  in_1,
  input  in_2,
  input  in_3,
  input  in_4,
  input  in_5,
  input  in_6,
  output S0,
  output S1,
  output S2,
  output S3,
  output N
);

  wire C1, S1_1, S1_2, S2_1;

  // _7408 7408_1: pin names not known; wires that end beside it: in_1, in_4, S0, in_2, in_4, S1_1, 1'b0, 1'b1, in_1, in_5, S1_2, in_2, in_5, S2_1
  // _7486 7486_1: pin names not known; wires that end beside it: S1_1, S1_2, S1, S2_1, C1, S2, 1'b0, 1'b1, in_3, in_6, N
  // _7408 7408_2: pin names not known; wires that end beside it: S1_1, S1_2, C1, C1, S2_1, S3, 1'b0, 1'b1

  // Other names for the same wires on the sheet: A0 = in_1; A1 = in_2; B0 = in_4; B1 = in_5; N0 = in_3; N1 = in_6
endmodule

module Division (
  input  in_1,
  input  in_2,
  input  in_3,
  input  in_4,
  input  in_5,
  input  in_6,
  output S0,
  output S1,
  output zero_divider_flag,
  output N
);

  wire minus_A0, minus_A1, minus_B0, minus_S0_1, S0_1, S0_2, S1_1, S1_2;

  // _7408 7408_1: pin names not known; wires that end beside it: in_1, in_5, S0_1, minus_S0_1, S0_2, S0, 1'b0, 1'b1, in_2, in_4, S0_2, in_2, in_1, S1_1
  // _7404 7404_1: pin names not known; wires that end beside it: in_1, minus_A0, S0_1, minus_S0_1, in_4, minus_B0, 1'b0, 1'b1, in_2, minus_A1
  // _7408 7408_2: pin names not known; wires that end beside it: S1_1, S1_2, S1, in_5, minus_B0, S1_2, 1'b0, 1'b1, minus_A0, minus_A1, zero_divider_flag

  assign N = in_6;

  // Other names for the same wires on the sheet: A0 = in_1; A1 = in_2; B0 = in_4; B1 = in_5; N0 = in_3; N1 = in_6;
  //   zero_divider = zero_divider_flag
endmodule

module Addition (
  input  in_1,
  input  in_2,
  input  in_3,
  input  in_4,
  input  in_5,
  input  in_6,
  output out_7,
  output out_8,
  output out_9,
  output out_10
);

  wire A0_F, A1_F, B0_F, B1_F, C0, C1, C1_2, C2, CTRL1, CTRL2, CTRL3, minus_C2, minus_CTRL3, minus_N0,
       minus_N1, minus_N_xor, N, N_xor, S0, S0_F, S1, S1_F;

  // _7408 7408_1: pin names not known; wires that end beside it: in_3, minus_N1, CTRL1, minus_N0, in_6, CTRL2, 1'b0, 1'b1, C0, minus_C2, CTRL3, minus_N_xor, C2, out_9
  // _7432 7432_1: pin names not known; wires that end beside it: CTRL2, CTRL1, C0, 1'b0, 1'b1, CTRL1, CTRL2, N_xor, CTRL3, N, out_10
  Full_adder full_adder_1 (.A(C0), .B(A0_F), .C(B0_F), .S(S0), .C_2(C1));
  Full_adder full_adder_2 (.A(C1), .B(A1_F), .C(B1_F), .S(S1), .C_2(C2));
  // _7404 7404_1: pin names not known; wires that end beside it: in_6, minus_N1, in_3, minus_N0, C2, minus_C2, 1'b0, 1'b1, CTRL3, minus_CTRL3, N_xor, minus_N_xor
  // _7486 7486_1: pin names not known; wires that end beside it: in_1, CTRL1, A0_F, in_2, CTRL1, A1_F, 1'b0, 1'b1, in_4, CTRL2, B0_F, in_5, CTRL2, B1_F
  Full_adder full_adder_3 (.A(CTRL3), .B(S0_F), .C(1'b0), .S(out_7), .C_2(C1_2));
  Full_adder full_adder_4 (.A(C1_2), .B(S1_F), .C(1'b0), .S(out_8));  // open: C_2
  // _7486 7486_2: pin names not known; wires that end beside it: S0, CTRL3, S0_F, S1, CTRL3, S1_F, 1'b0, 1'b1, in_3, in_6
  and and_1 (N, in_6, in_3);

  // Other names for the same wires on the sheet: A0 = in_1; A1 = in_2; B0 = in_4; B1 = in_5; N0 = in_3; N1 = in_6;
  //   N_F = out_10; S0_FF = out_7; S1_FF = out_8; S2_FF = out_9
endmodule

// F adder
module Full_adder (
  input  A,
  input  B,
  input  C,
  output S,
  output C_2
);

  wire half_adder_1_c, half_adder_1_s, half_adder_2_c;

  Half_adder half_adder_1 (.A(A), .B(B), .S(half_adder_1_s), .C(half_adder_1_c));
  Half_adder half_adder_2 (.A(half_adder_1_s), .B(C), .S(S), .C(half_adder_2_c));
  or or_1 (C_2, half_adder_1_c, half_adder_2_c);
endmodule

module Half_adder (
  input  A,
  input  B,
  output S,
  output C
);

  xor xor_1 (S, A, B);
  and and_1 (C, A, B);
endmodule

module main (
  input  in_1,
  input  in_2,
  input  in_3,
  input  in_4,
  input  in_5,
  input  in_6,
  input  in_7,
  input  in_8
);

  wire addition_1_out_7, addition_1_out_8, addition_1_out_9, addition_1_out_10, n7432_1_p2, n7448_1_p10,
       n7448_1_p11, n7448_1_p12, n7448_1_p13, n7448_1_p14, n7448_1_p15, n7448_1_p16, n74157_1_p3,
       n74157_1_p4, n74157_1_p8, n74157_1_p9, n74157_1_p10, n74157_2_p2, n74157_2_p4, n74157_2_p5,
       n74157_2_p7, n74157_2_p11, n74157_2_p13, n74157_2_p14, n74157_2_p16, n74157_3_p2, n74157_3_p4,
       n74157_3_p5, n74157_3_p13, n74157_4_p3, n74157_4_p4, n74157_4_p6, n74157_4_p7, n74157_4_p12,
       n74157_4_p13, n74157_4_p15, n74157_5_p2, n74157_5_p5, n74157_5_p11, n74157_5_p14, not_1_out,
       remainder_1_out_10, remainder_1_y, remainder_1_z, zero_flag_1_out_5;

  // _74157 74157_1: pin names not known; wires that end beside it: in_7, 1'b0, n74157_1_p3, n74157_1_p4, 1'b0, 1'b1, 1'b0, n74157_1_p8, n74157_1_p9, n74157_1_p10
  Remainder remainder_1 (
    .A(in_1), .B(in_2), .C(in_3), .D(in_4), .E(in_5), .F(in_6), .N(n74157_1_p9), .Y(remainder_1_y),
    .Z(remainder_1_z), .out_10(remainder_1_out_10));
  // _74157 74157_2: pin names not known; wires that end beside it: in_7, n74157_2_p2, remainder_1_z, n74157_2_p4, n74157_2_p5, remainder_1_y, n74157_2_p7, 1'b0, 1'b1, 1'b0, n74157_2_p11, 1'b0, n74157_2_p13, n74157_2_p14, 1'b0, n74157_2_p16
  // _74157 74157_3: pin names not known; wires that end beside it: in_8, n74157_3_p2, 1'b0, n74157_3_p4, n74157_3_p5, 1'b0, n74157_1_p8, 1'b0, 1'b1, 1'b0, 1'b0, n74157_3_p2, n74157_3_p13, remainder_1_out_10, 1'b0, n74157_1_p3
  Multiplier multiplier_1 (
    .A(in_1), .B(in_2), .C(in_3), .D(in_4), .E(in_5), .F(in_6), .N(n74157_3_p5), .W(n74157_2_p14),
    .X(n74157_2_p11), .Y(n74157_2_p5), .Z(n74157_2_p2));
  // _74157 74157_4: pin names not known; wires that end beside it: in_8, n74157_2_p4, n74157_4_p3, n74157_4_p4, n74157_2_p7, n74157_4_p6, n74157_4_p7, 1'b0, 1'b1, 1'b0, n74157_2_p13, n74157_4_p12, n74157_4_p13, n74157_2_p16, n74157_4_p15, n74157_3_p2
  // _7432 7432_1: pin names not known; wires that end beside it: 1'b0, n7432_1_p2, n74157_3_p13, n74157_1_p10, 1'b1
  addition addition_1 (
    .A(in_6), .B(in_5), .C(in_4), .D(in_3), .E(in_2), .F(in_1), .out_7(addition_1_out_7),
    .out_8(addition_1_out_8), .out_9(addition_1_out_9), .out_10(addition_1_out_10));
  // _74157 74157_5: pin names not known; wires that end beside it: in_7, n74157_5_p2, addition_1_out_7, n74157_4_p3, n74157_5_p5, addition_1_out_8, n74157_4_p6, 1'b0, 1'b1, 1'b0, n74157_5_p11, addition_1_out_9, n74157_4_p12, n74157_5_p14, addition_1_out_10, n74157_4_p15
  // _7448 7448_1: pin names not known; wires that end beside it: n74157_4_p7, n74157_4_p13, 1'b1, 1'b1, 1'b1, n74157_3_p4, n74157_4_p4, 1'b0, 1'b1, n7448_1_p10, n7448_1_p11, n7448_1_p12, n7448_1_p13, n7448_1_p14, n7448_1_p15, n7448_1_p16
  not not_1 (not_1_out, in_4);
  addition addition_2 (
    .A(in_6), .B(in_5), .C(not_1_out), .D(in_3), .E(in_2), .F(in_1), .out_7(n74157_5_p2),
    .out_8(n74157_5_p5), .out_9(n74157_5_p11), .out_10(n74157_5_p14));
  zero_flag zero_flag_1 (
    .in_1(n74157_4_p4), .in_2(n74157_4_p7), .in_3(n74157_4_p13), .in_4(n74157_3_p2), .out_5(zero_flag_1_out_5));
  _7_Segment_Display u_7_segment_display_1 (.g(n7432_1_p2));  // open: f, a, b, e, d, c, dp
  _7_Segment_Display u_7_segment_display_2 (
    .g(n7448_1_p11), .f(n7448_1_p10), .a(n7448_1_p12), .b(n7448_1_p13), .e(n7448_1_p16), .d(n7448_1_p15),
    .c(n7448_1_p14));  // open: dp
  LED led_1 (.in(zero_flag_1_out_5));
  LED led_2 (.in(n74157_1_p4));

  // Notes on the sheet:
  //   1
  //   0
  //   0
  //   1
  //   1
  //   0
  //   multiplication
  //   subtraction
  //   1
  //   remainder
  //   0
  //   addition
  //   ZERO FLAG
  //   DIVISION BY ZERO
endmodule

module Remainder (
  input  A,
  input  B,
  input  C,
  input  D,
  input  E,
  input  F,
  output N,
  output Y,
  output Z,
  output out_10
);

  wire n7404_1_p2, n7404_1_p9, n7404_1_p11, n7408_1_p3, n7408_1_p6, n7408_1_p8, n7408_1_p10, n7408_1_p11,
       n7408_1_p12, n7408_2_p9;

  // _7408 7408_1: pin names not known; wires that end beside it: 1'b0, Y, n7408_1_p3, n7408_1_p3, F, n7408_1_p6, E, n7408_1_p8, n7408_1_p6, n7408_1_p10, n7408_1_p11, n7408_1_p12, B, 1'b1
  // _7404 7404_1: pin names not known; wires that end beside it: 1'b0, n7404_1_p2, n7408_1_p8, n7408_1_p12, n7408_1_p11, Y, C, n7408_1_p10, n7404_1_p9, Z, n7404_1_p11, 1'b1
  // _7408 7408_2: pin names not known; wires that end beside it: 1'b0, N, n7404_1_p11, A, B, n7404_1_p2, F, Z, n7408_2_p9, n7404_1_p9, C, n7408_2_p9, D, E, 1'b1
  // _7402 7402_1: pin names not known; wires that end beside it: 1'b0, E, F, out_10, 1'b1
endmodule

module Multiplier (
  input  A,
  input  B,
  input  C,
  input  D,
  input  E,
  input  F,
  output N,
  output W,
  output X,
  output Y,
  output Z
);

  wire n7408_1_p3, n7408_1_p4, n7408_2_p3, n7408_2_p4, n7408_2_p5, n7408_2_p7, n7432_1_p3, n7432_1_p7;

  // _7408 7408_1: pin names not known; wires that end beside it: 1'b0, 1'b1, n7408_1_p3, n7408_1_p4, N
  // _7408 7408_2: pin names not known; wires that end beside it: 1'b0, 1'b1, n7408_2_p3, n7408_2_p4, n7408_2_p5, n7408_2_p5, n7408_2_p7, W
  // _7432 7432_1: pin names not known; wires that end beside it: 1'b0, n7408_1_p3, n7432_1_p3, W, X, n7432_1_p3, n7432_1_p7, n7432_1_p7, Y, Z, 1'b1
  // _7408 7408_3: pin names not known; wires that end beside it: 1'b1, B, C, E, E, n7408_2_p7, n7408_2_p3, B, C, F, F, n7408_2_p4, Z, 1'b0
  // _7486 7486_1: pin names not known; wires that end beside it: n7408_2_p3, n7408_2_p4, Y, n7408_2_p5, n7408_2_p7, X, 1'b0, 1'b1, A, D, n7408_1_p4
endmodule

module zero_flag (
  input  in_1,
  input  in_2,
  input  in_3,
  input  in_4,
  output out_5
);

  wire n7432_1_p2, n7432_1_p3, n7432_1_p7;

  // _7432 7432_1: pin names not known; wires that end beside it: 1'b0, n7432_1_p2, n7432_1_p3, in_4, in_3, n7432_1_p3, n7432_1_p7, n7432_1_p7, in_2, in_1, 1'b1
  not not_1 (out_5, n7432_1_p2);
endmodule
