// Logisim project adder and subtractor(final).circ as structural Verilog: 9 circuits, main circuit addition
module half (
  input  in_1,
  input  in_2,
  output out_3,
  output out_4
);

  xor xor_1 (out_3, in_1, in_2);
  and and_1 (out_4, in_1, in_2);
endmodule

module full (
  input  in_1,
  input  in_2,
  input  in_3,
  output out_4,
  output out_5
);

  wire half_1_out_3, half_1_out_4, half_2_out_4;

  half half_1 (.in_1(in_1), .in_2(in_2), .out_3(half_1_out_3), .out_4(half_1_out_4));
  half half_2 (.in_1(half_1_out_3), .in_2(in_3), .out_3(out_4), .out_4(half_2_out_4));
  or or_1 (out_5, half_2_out_4, half_1_out_4);
endmodule

module complement (
  input  in_1,
  input  in_2,
  input  in_3,
  output out_4,
  output out_5,
  output out_6
);

  wire half_1_out_4, half_2_out_4, not_1_out, not_2_out, not_3_out;

  not not_1 (not_1_out, in_1);
  not not_2 (not_2_out, in_2);
  half half_1 (.in_1(1'b1), .in_2(not_1_out), .out_3(out_4), .out_4(half_1_out_4));
  not not_3 (not_3_out, in_3);
  half half_2 (.in_1(half_1_out_4), .in_2(not_2_out), .out_3(out_5), .out_4(half_2_out_4));
  half half_3 (.in_1(half_2_out_4), .in_2(not_3_out), .out_3(out_6));  // open: out_4
endmodule

module test (
  input  in_1,
  input  in_2,
  input  in_3,
  input  in_4,
  output out_5,
  output out_6,
  output out_7
);

  wire complement_1_out_4, complement_1_out_5, complement_1_out_6;

  complement complement_1 (
    .in_1(in_1), .in_2(in_2), .in_3(in_3), .out_4(complement_1_out_4), .out_5(complement_1_out_5),
    .out_6(complement_1_out_6));
  // _74157 74157_1: pin names not known; wires that end beside it: in_4, in_1, complement_1_out_4, out_5, in_2, complement_1_out_5, out_6, 1'b0, 1'b1, 1'b0, in_3, complement_1_out_6, out_7
endmodule

module checker_2 (
  input  in_1,
  input  in_2,
  input  in_3,
  input  in_4,
  input  in_5,
  output out_6,
  output out_7,
  output out_8,
  output out_9
);

  wire complement_1_out_4, complement_1_out_5, complement_1_out_6, n74157_1_p4, n74157_1_p7, n74157_1_p13,
       n74157_1_p16;

  complement complement_1 (
    .in_1(in_1), .in_2(in_2), .in_3(in_3), .out_4(complement_1_out_4), .out_5(complement_1_out_5),
    .out_6(complement_1_out_6));
  // _74157 74157_1: pin names not known; wires that end beside it: in_3, complement_1_out_4, in_1, n74157_1_p4, complement_1_out_5, in_2, n74157_1_p7, 1'b0, 1'b1, 1'b0, 1'b0, 1'b0, n74157_1_p13, complement_1_out_6, in_4, n74157_1_p16
  // _74157 74157_2: pin names not known; wires that end beside it: in_5, in_1, n74157_1_p4, out_6, in_2, n74157_1_p7, out_7, 1'b0, 1'b1, 1'b0, in_3, n74157_1_p13, out_8, in_4, n74157_1_p16, out_9
endmodule

module subtraction (
  input  A,
  input  B,
  input  C,
  input  D,
  input  E,
  input  F,
  output out_7,
  output out_8,
  output out_9,
  output out_10
);

  wire full_1_out_4, full_1_out_5, full_2_out_4, full_2_out_5, half_1_out_3, half_1_out_4, n7408_1_p3,
       n7408_1_p6, n7486_1_p3, not_1_out, test_1_out_5, test_1_out_6, test_1_out_7, test_2_out_5,
       test_2_out_6, test_2_out_7;

  not not_1 (not_1_out, C);
  // _7486 7486_1: pin names not known; wires that end beside it: not_1_out, F, n7486_1_p3, 1'b0, 1'b1
  test test_1 (
    .in_1(A), .in_2(B), .in_3(not_1_out), .in_4(n7408_1_p3), .out_5(test_1_out_5), .out_6(test_1_out_6),
    .out_7(test_1_out_7));
  // _7408 7408_1: pin names not known; wires that end beside it: not_1_out, n7486_1_p3, n7408_1_p3, F, n7486_1_p3, n7408_1_p6, 1'b0, 1'b1
  test test_2 (
    .in_1(D), .in_2(E), .in_3(F), .in_4(n7408_1_p6), .out_5(test_2_out_5), .out_6(test_2_out_6),
    .out_7(test_2_out_7));
  half half_1 (.in_1(test_1_out_5), .in_2(test_2_out_5), .out_3(half_1_out_3), .out_4(half_1_out_4));
  full full_1 (
    .in_1(half_1_out_4), .in_2(test_1_out_6), .in_3(test_2_out_6), .out_4(full_1_out_4), .out_5(full_1_out_5));
  full full_2 (
    .in_1(full_1_out_5), .in_2(test_1_out_7), .in_3(test_2_out_7), .out_4(full_2_out_4), .out_5(full_2_out_5));
  checker_2 checker_2_1 (
    .in_1(half_1_out_3), .in_2(full_1_out_4), .in_3(full_2_out_4), .in_4(full_2_out_5), .in_5(n7486_1_p3),
    .out_6(out_7), .out_7(out_8), .out_8(out_9), .out_9(out_10));
endmodule

module addition (
  input  A,
  input  B,
  input  C,
  input  D,
  input  E,
  input  F,
  output out_7,
  output out_8,
  output out_9,
  output out_10
);

  wire full_1_out_4, full_1_out_5, full_2_out_4, full_2_out_5, half_1_out_3, half_1_out_4, n7408_1_p3,
       n7408_1_p6, n7486_1_p3, test_1_out_5, test_1_out_6, test_1_out_7, test_2_out_5, test_2_out_6,
       test_2_out_7;

  // _7486 7486_1: pin names not known; wires that end beside it: C, F, n7486_1_p3, 1'b0, 1'b1
  test test_1 (
    .in_1(A), .in_2(B), .in_3(C), .in_4(n7408_1_p3), .out_5(test_1_out_5), .out_6(test_1_out_6),
    .out_7(test_1_out_7));
  // _7408 7408_1: pin names not known; wires that end beside it: C, n7486_1_p3, n7408_1_p3, F, n7486_1_p3, n7408_1_p6, 1'b0, 1'b1
  test test_2 (
    .in_1(D), .in_2(E), .in_3(F), .in_4(n7408_1_p6), .out_5(test_2_out_5), .out_6(test_2_out_6),
    .out_7(test_2_out_7));
  half half_1 (.in_1(test_1_out_5), .in_2(test_2_out_5), .out_3(half_1_out_3), .out_4(half_1_out_4));
  full full_1 (
    .in_1(half_1_out_4), .in_2(test_1_out_6), .in_3(test_2_out_6), .out_4(full_1_out_4), .out_5(full_1_out_5));
  full full_2 (
    .in_1(full_1_out_5), .in_2(test_1_out_7), .in_3(test_2_out_7), .out_4(full_2_out_4), .out_5(full_2_out_5));
  checker_2 checker_2_1 (
    .in_1(half_1_out_3), .in_2(full_1_out_4), .in_3(full_2_out_4), .in_4(full_2_out_5), .in_5(n7486_1_p3),
    .out_6(out_7), .out_7(out_8), .out_8(out_9), .out_9(out_10));
endmodule

module addition_2_0 (
  input  in_1,
  input  in_2,
  input  in_3,
  input  in_4,
  input  in_5,
  input  in_6,
  output out_7,
  output out_8,
  output out_9,
  output out_10
);

  wire and_1_out, complement_2_0_1_out_3, complement_2_0_1_out_4, complement_2_0_2_out_3,
       complement_2_0_2_out_4, complement_2_0_3_out_3, complement_2_0_3_out_4, full_1_out_4, full_1_out_5,
       half_1_out_3, half_1_out_4, n7408_1_p3, n7432_1_p3, n7432_1_p8, n7432_2_p3, n7432_2_p4, n7432_2_p6,
       n74157_1_p4, n74157_1_p7, n74157_2_p1, n74157_2_p4, n74157_2_p7, n74157_3_p13, not_1_out, not_2_out,
       or_1_out, xor_1_out;

  // _7432 7432_1: pin names not known; wires that end beside it: in_4, in_5, n7432_1_p3, 1'b0, 1'b1, in_1, in_2, n7432_1_p8
  complement_2_0 complement_2_0_1 (
    .in_1(in_1), .in_2(in_2), .out_3(complement_2_0_1_out_3), .out_4(complement_2_0_1_out_4));
  complement_2_0 complement_2_0_2 (
    .in_1(in_4), .in_2(in_5), .out_3(complement_2_0_2_out_3), .out_4(complement_2_0_2_out_4));
  // _74157 74157_1: pin names not known; wires that end beside it: in_3, in_1, complement_2_0_1_out_3, n74157_1_p4, in_2, complement_2_0_1_out_4, n74157_1_p7, 1'b0, 1'b1, 1'b0
  // _74157 74157_2: pin names not known; wires that end beside it: n74157_2_p1, in_4, complement_2_0_2_out_3, n74157_2_p4, in_5, complement_2_0_2_out_4, n74157_2_p7, 1'b0, 1'b1, 1'b0
  // _7408 7408_1: pin names not known; wires that end beside it: in_3, n7432_1_p8, n7408_1_p3, n7432_1_p3, in_6, n74157_2_p1, 1'b0, 1'b1
  half half_1 (.in_1(n74157_1_p4), .in_2(n74157_2_p4), .out_3(half_1_out_3), .out_4(half_1_out_4));
  full full_1 (.in_1(n74157_1_p7), .in_2(n74157_2_p7), .in_3(half_1_out_4), .out_4(full_1_out_4), .out_5(full_1_out_5));
  complement_2_0 complement_2_0_3 (
    .in_1(half_1_out_3), .in_2(full_1_out_4), .out_3(complement_2_0_3_out_3), .out_4(complement_2_0_3_out_4));
  xor xor_1 (xor_1_out, n74157_2_p1, n7408_1_p3);
  not not_1 (not_1_out, full_1_out_5);
  and and_1 (and_1_out, not_1_out, xor_1_out);
  // _7432 7432_2: pin names not known; wires that end beside it: n7408_1_p3, n74157_2_p1, n7432_2_p3, n7432_2_p4, out_9, n7432_2_p6, 1'b0, 1'b1, out_7, out_8, n7432_2_p4
  // _74157 74157_3: pin names not known; wires that end beside it: and_1_out, half_1_out_3, complement_2_0_3_out_3, out_7, full_1_out_4, complement_2_0_3_out_4, out_8, 1'b0, 1'b1, 1'b0, full_1_out_5, 1'b0, n74157_3_p13
  not not_2 (not_2_out, n7432_2_p3);
  or or_1 (or_1_out, n7432_2_p4, not_2_out);
  and and_2 (out_9, n74157_3_p13, or_1_out);
  and and_3 (out_10, and_1_out, n7432_2_p6);
endmodule

module complement_2_0 (
  input  in_1,
  input  in_2,
  output out_3,
  output out_4
);

  xor xor_1 (out_4, in_1, in_2);

  assign out_3 = in_1;
endmodule
