// Logisim project adder and subtractor(final).circ as structural Verilog: 7 circuits, main circuit adittion
module half (
  input  in_1,
  input  in_2,
  output out_3,
  output out_4
);

  xor xor_1 (out_3, in_1, in_2);
  and and_1 (out_4, in_1, in_2);
endmodule

module full (
  input  in_1,
  input  in_2,
  input  in_3,
  output out_4,
  output out_5
);

  wire half_1_out_3, half_1_out_4, half_2_out_4;

  half half_1 (.in_1(in_1), .in_2(in_2), .out_3(half_1_out_3), .out_4(half_1_out_4));
  half half_2 (.in_1(half_1_out_3), .in_2(in_3), .out_3(out_4), .out_4(half_2_out_4));
  or or_1 (out_5, half_2_out_4, half_1_out_4);
endmodule

module complement (
  input  in_1,
  input  in_2,
  input  in_3,
  output out_4,
  output out_5,
  output out_6
);

  wire and_1_out, and_2_out, and_3_out, not_1_out, not_2_out, not_3_out, not_4_out;

  not not_1 (not_1_out, in_3);
  not not_2 (not_2_out, in_1);
  not not_3 (not_3_out, in_2);
  xor xor_1 (out_5, in_1, in_2);
  and and_1 (and_1_out, in_1, not_1_out);
  not not_4 (not_4_out, in_3);
  and and_2 (and_2_out, not_2_out, not_3_out, in_3);
  and and_3 (and_3_out, not_2_out, in_2, not_4_out);
  or or_1 (out_6, and_1_out, and_2_out, and_3_out);

  assign out_4 = in_1;
endmodule

module test (
  input  in_1,
  input  in_2,
  input  in_3,
  input  in_4,
  output out_5,
  output out_6,
  output out_7
);

  wire complement_1_out_4, complement_1_out_5, complement_1_out_6;

  complement complement_1 (
    .in_1(in_1), .in_2(in_2), .in_3(in_3), .out_4(complement_1_out_4), .out_5(complement_1_out_5),
    .out_6(complement_1_out_6));
  // _74157 74157_1: pin names not known; wires that end beside it: in_4, in_1, complement_1_out_4, out_5, in_2, complement_1_out_5, out_6, 1'b0, 1'b1, 1'b0, in_3, complement_1_out_6, out_7
endmodule

module cheker_2 (
  input  in_1,
  input  in_2,
  input  in_3,
  input  in_4,
  input  in_5,
  output out_6,
  output out_7,
  output out_8,
  output out_9
);

  wire complement_1_out_4, complement_1_out_5, complement_1_out_6, n74157_1_p4, n74157_1_p7, n74157_1_p13,
       n74157_1_p16;

  complement complement_1 (
    .in_1(in_1), .in_2(in_2), .in_3(in_3), .out_4(complement_1_out_4), .out_5(complement_1_out_5),
    .out_6(complement_1_out_6));
  // _74157 74157_1: pin names not known; wires that end beside it: in_3, complement_1_out_4, in_1, n74157_1_p4, complement_1_out_5, in_2, n74157_1_p7, 1'b0, 1'b1, 1'b0, 1'b0, 1'b0, n74157_1_p13, complement_1_out_6, in_4, n74157_1_p16
  // _74157 74157_2: pin names not known; wires that end beside it: in_5, in_1, n74157_1_p4, out_6, in_2, n74157_1_p7, out_7, 1'b0, 1'b1, 1'b0, in_3, n74157_1_p13, out_8, in_4, n74157_1_p16, out_9
endmodule

module subtraction (
  input  A,
  input  B,
  input  C,
  input  D,
  input  E,
  input  F
);

  wire cheker_2_1_out_6, cheker_2_1_out_7, cheker_2_1_out_8, cheker_2_1_out_9, full_1_out_4, full_1_out_5,
       full_2_out_4, full_2_out_5, half_1_out_3, half_1_out_4, n7408_1_p3, n7408_1_p6, n7448_1_p10,
       n7448_1_p11, n7448_1_p12, n7448_1_p13, n7448_1_p14, n7448_1_p15, n7448_1_p16, n7486_1_p3, not_1_out,
       test_1_out_5, test_1_out_6, test_1_out_7, test_2_out_5, test_2_out_6, test_2_out_7;

  not not_1 (not_1_out, F);
  // _7486 7486_1: pin names not known; wires that end beside it: C, not_1_out, n7486_1_p3, 1'b0, 1'b1
  test test_1 (
    .in_1(A), .in_2(B), .in_3(C), .in_4(n7408_1_p3), .out_5(test_1_out_5), .out_6(test_1_out_6),
    .out_7(test_1_out_7));
  // _7408 7408_1: pin names not known; wires that end beside it: C, n7486_1_p3, n7408_1_p3, not_1_out, n7486_1_p3, n7408_1_p6, 1'b0, 1'b1
  test test_2 (
    .in_1(D), .in_2(E), .in_3(not_1_out), .in_4(n7408_1_p6), .out_5(test_2_out_5), .out_6(test_2_out_6),
    .out_7(test_2_out_7));
  half half_1 (.in_1(test_1_out_5), .in_2(test_2_out_5), .out_3(half_1_out_3), .out_4(half_1_out_4));
  full full_1 (
    .in_1(half_1_out_4), .in_2(test_1_out_6), .in_3(test_2_out_6), .out_4(full_1_out_4), .out_5(full_1_out_5));
  full full_2 (
    .in_1(full_1_out_5), .in_2(test_1_out_7), .in_3(test_2_out_7), .out_4(full_2_out_4), .out_5(full_2_out_5));
  cheker_2 cheker_2_1 (
    .in_1(half_1_out_3), .in_2(full_1_out_4), .in_3(full_2_out_4), .in_4(full_2_out_5), .in_5(n7486_1_p3),
    .out_6(cheker_2_1_out_6), .out_7(cheker_2_1_out_7), .out_8(cheker_2_1_out_8), .out_9(cheker_2_1_out_9));
  // _7448 7448_1: pin names not known; wires that end beside it: cheker_2_1_out_7, cheker_2_1_out_8, 1'b1, 1'b1, 1'b1, 1'b0, cheker_2_1_out_6, 1'b0, 1'b1, n7448_1_p10, n7448_1_p11, n7448_1_p12, n7448_1_p13, n7448_1_p14, n7448_1_p15, n7448_1_p16
  LED led_1 (.in(cheker_2_1_out_9));
  _7_Segment_Display u_7_segment_display_1 (
    .g(n7448_1_p11), .f(n7448_1_p10), .a(n7448_1_p12), .b(n7448_1_p13), .e(n7448_1_p16), .d(n7448_1_p15),
    .c(n7448_1_p14));  // open: dp
endmodule

module adittion (
  input  A,
  input  B,
  input  C,
  input  D,
  input  E,
  input  F
);

  wire cheker_2_1_out_6, cheker_2_1_out_7, cheker_2_1_out_8, cheker_2_1_out_9, full_1_out_4, full_1_out_5,
       full_2_out_4, full_2_out_5, half_1_out_3, half_1_out_4, n7408_1_p3, n7408_1_p6, n7448_1_p10,
       n7448_1_p11, n7448_1_p12, n7448_1_p13, n7448_1_p14, n7448_1_p15, n7448_1_p16, n7486_1_p3,
       test_1_out_5, test_1_out_6, test_1_out_7, test_2_out_5, test_2_out_6, test_2_out_7;

  // _7486 7486_1: pin names not known; wires that end beside it: C, F, n7486_1_p3, 1'b0, 1'b1
  test test_1 (
    .in_1(A), .in_2(B), .in_3(C), .in_4(n7408_1_p3), .out_5(test_1_out_5), .out_6(test_1_out_6),
    .out_7(test_1_out_7));
  // _7408 7408_1: pin names not known; wires that end beside it: C, n7486_1_p3, n7408_1_p3, F, n7486_1_p3, n7408_1_p6, 1'b0, 1'b1
  test test_2 (
    .in_1(D), .in_2(E), .in_3(F), .in_4(n7408_1_p6), .out_5(test_2_out_5), .out_6(test_2_out_6),
    .out_7(test_2_out_7));
  half half_1 (.in_1(test_1_out_5), .in_2(test_2_out_5), .out_3(half_1_out_3), .out_4(half_1_out_4));
  full full_1 (
    .in_1(half_1_out_4), .in_2(test_1_out_6), .in_3(test_2_out_6), .out_4(full_1_out_4), .out_5(full_1_out_5));
  full full_2 (
    .in_1(full_1_out_5), .in_2(test_1_out_7), .in_3(test_2_out_7), .out_4(full_2_out_4), .out_5(full_2_out_5));
  cheker_2 cheker_2_1 (
    .in_1(half_1_out_3), .in_2(full_1_out_4), .in_3(full_2_out_4), .in_4(full_2_out_5), .in_5(n7486_1_p3),
    .out_6(cheker_2_1_out_6), .out_7(cheker_2_1_out_7), .out_8(cheker_2_1_out_8), .out_9(cheker_2_1_out_9));
  // _7448 7448_1: pin names not known; wires that end beside it: cheker_2_1_out_7, cheker_2_1_out_8, 1'b1, 1'b1, 1'b1, 1'b0, cheker_2_1_out_6, 1'b0, 1'b1, n7448_1_p10, n7448_1_p11, n7448_1_p12, n7448_1_p13, n7448_1_p14, n7448_1_p15, n7448_1_p16
  LED led_1 (.in(cheker_2_1_out_9));
  _7_Segment_Display u_7_segment_display_1 (
    .g(n7448_1_p11), .f(n7448_1_p10), .a(n7448_1_p12), .b(n7448_1_p13), .e(n7448_1_p16), .d(n7448_1_p15),
    .c(n7448_1_p14));  // open: dp
endmodule
