// Logisim project remainder.circ as structural Verilog: 1 circuit, main circuit Remainder
module Remainder (
  input  A,
  input  B,
  input  C,
  input  D,
  input  E,
  input  F,
  output out_7,
  output out_8,
  output out_9
);

  wire n7404_1_p2, n7404_1_p9, n7404_1_p11, n7408_1_p3, n7408_1_p6, n7408_1_p8, n7408_1_p10, n7408_1_p11,
       n7408_1_p12, n7408_2_p9;

  // _7408 7408_1: pin names not known; wires that end beside it: 1'b0, out_8, n7408_1_p3, n7408_1_p3, F, n7408_1_p6, E, n7408_1_p8, n7408_1_p6, n7408_1_p10, n7408_1_p11, n7408_1_p12, B, 1'b1
  // _7404 7404_1: pin names not known; wires that end beside it: 1'b0, n7404_1_p2, n7408_1_p8, n7408_1_p12, n7408_1_p11, out_8, C, n7408_1_p10, n7404_1_p9, out_9, n7404_1_p11, 1'b1
  // _7408 7408_2: pin names not known; wires that end beside it: 1'b0, out_7, n7404_1_p11, A, B, n7404_1_p2, F, out_9, n7408_2_p9, n7404_1_p9, C, n7408_2_p9, D, E, 1'b1
endmodule
